# Fritzing sketch esqueleto-murcielagos (saved by Fritzing 0.9.8b)
breadboards: 1

parts:
  LED_PRIM_CAJA = Adafruit Breadboard-Friendly NeoPixel [part_number="Adafruit #1312"]
  Nano_Esqueleto_Primario = Arduino Nano (Rev3.0)
  RDM6300_Prim_1 = IC, SIP package, 3 pins [chip_label=RFID]
  RDM6300_Prim_2 = IC, SIP package, 3 pins [chip_label=RFID]
  RDM6300_Prim_3 = IC, SIP package, 3 pins [chip_label=RFID]
  RDM6300_Prim_4 = IC, SIP package, 3 pins [chip_label=RFID]
  LED_PRIM_RAYOS = Adafruit Breadboard-Friendly NeoPixel [part_number="Adafruit #1312"]
  Rele_Prim = IC, SIP package, 3 pins [chip_label=Rele]
  Rele_Sec = IC, SIP package, 3 pins [chip_label=Rele]
  Nano_Esqueleto_Secundario = Arduino Nano (Rev3.0)
  RDM6300_Sec_1 = IC, SIP package, 3 pins [chip_label=RFID]
  RDM6300_Sec_3 = IC, SIP package, 3 pins [chip_label=RFID]
  RDM6300_Sec_4 = IC, SIP package, 3 pins [chip_label=RFID]
  RDM6300_Sec_2 = IC, SIP package, 3 pins [chip_label=RFID]
  LED_SEC_CAJA = Adafruit Breadboard-Friendly NeoPixel [part_number="Adafruit #1312"]
  LED_SEC_RAYOS = Adafruit Breadboard-Friendly NeoPixel [part_number="Adafruit #1312"]
  Nano_Murcielagos = Arduino Nano (Rev3.0)
  LED_OJOS_MURCIELAGOS = Adafruit Breadboard-Friendly NeoPixel [part_number="Adafruit #1312"]

nets:
  P10: LED_PRIM_CAJA.IN, Nano_Esqueleto_Primario.D10
  GND: LED_PRIM_CAJA.GND, Nano_Esqueleto_Primario.GND, RDM6300_Prim_1.pin3, RDM6300_Prim_2.pin3, RDM6300_Prim_3.pin3, RDM6300_Prim_4.pin3, LED_PRIM_RAYOS.GND, Rele_Prim.pin3, Rele_Sec.pin3, Nano_Esqueleto_Secundario.GND, RDM6300_Sec_1.pin3, RDM6300_Sec_3.pin3, RDM6300_Sec_4.pin3, RDM6300_Sec_2.pin3, LED_SEC_RAYOS.GND, Nano_Murcielagos.GND
  5V: LED_PRIM_CAJA.VDD, RDM6300_Prim_1.pin1, LED_PRIM_RAYOS.VDD, LED_SEC_RAYOS.VDD
  P2: Nano_Esqueleto_Primario.D2, RDM6300_Prim_1.pin2
  P4: Nano_Esqueleto_Primario.D4, RDM6300_Prim_2.pin2
  P6: Nano_Esqueleto_Primario.D6, RDM6300_Prim_3.pin2
  P8: Nano_Esqueleto_Primario.D8, RDM6300_Prim_4.pin2
  P11: Nano_Esqueleto_Primario.D11/MOSI, LED_PRIM_RAYOS.IN
  P12: Nano_Esqueleto_Primario.D12/MISO, Rele_Prim.pin2
  M12: Nano_Esqueleto_Primario.A3, Nano_Esqueleto_Secundario.A0, Nano_Murcielagos.D12/MISO
  M11: Nano_Esqueleto_Primario.A2, Nano_Murcielagos.D11/MOSI
  S12: Nano_Esqueleto_Primario.A1, Nano_Esqueleto_Secundario.D12/MISO
  PA0: Nano_Esqueleto_Primario.A0, Rele_Sec.pin2
  S2: Nano_Esqueleto_Secundario.D2, RDM6300_Sec_1.pin2
  S4: Nano_Esqueleto_Secundario.D4, RDM6300_Sec_2.pin2
  S6: Nano_Esqueleto_Secundario.D6, RDM6300_Sec_3.pin2
  S8: Nano_Esqueleto_Secundario.D8, RDM6300_Sec_4.pin2
  S10: Nano_Esqueleto_Secundario.D10, LED_SEC_CAJA.IN
  S11: Nano_Esqueleto_Secundario.D11/MOSI, LED_SEC_RAYOS.IN
  M2: Nano_Murcielagos.D2
  M3: Nano_Murcielagos.D3
  M4: Nano_Murcielagos.D4
  M5: Nano_Murcielagos.D5
  M6: Nano_Murcielagos.D6
  M7: Nano_Murcielagos.D7
  M8: Nano_Murcielagos.D8
  M10: Nano_Murcielagos.D10, LED_OJOS_MURCIELAGOS.IN
  MA6: Nano_Murcielagos.A6
  MA5: Nano_Murcielagos.A5
  MA4: Nano_Murcielagos.A4
  MA3: Nano_Murcielagos.A3
  MA2: Nano_Murcielagos.A2
  MA1: Nano_Murcielagos.A1
  MA0: Nano_Murcielagos.A0

notes:
  S12: Pin con el que el Secundario indica al Primario que se ha completado la fase RFID.
  Acordarse de conectar el pin TX (transmisión) de los RFID, no el RX (recepción).
  M11: Pin con el que el Primario indica a los Murcielagos que pueden activarse.
  M12: Pin con el que los Murcielagos indican al Primario y Secundario que se han completado.
  MA0-MA6: Pines de los sensores de los muercielagos.
  M2-M8: Pines de los altavoces de murcielagos.

custom parts:
  Adafruit Breadboard-Friendly NeoPixel: This is the easiest way possible to add small, bright RGB pixels to your project. We took the same technology from our Flora NeoPixels and made them breadboard friendly, with two rows of 3 x 0.1" spaced header on each side for easy soldering, chaining and breadboarding. These ultra-bright LEDs have a constant-current driver cooked right into the LED package! The pixels are chainable - so you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
