# Fritzing sketch esqueletos (saved by Fritzing 0.9.8b)
breadboards: 1

parts:
  LED_PRIM_CAJA = Adafruit Breadboard-Friendly NeoPixel [part_number="Adafruit #1312"]
  Nano_Esqueleto_Primario = Arduino Nano (Rev3.0)
  RDM6300_Prim_1 = IC, SIP package, 3 pins [chip_label=RFID]
  RDM6300_Prim_2 = IC, SIP package, 3 pins [chip_label=RFID]
  RDM6300_Prim_3 = IC, SIP package, 3 pins [chip_label=RFID]
  RDM6300_Prim_4 = IC, SIP package, 3 pins [chip_label=RFID]
  LED_PRIM_RAYOS = Adafruit Breadboard-Friendly NeoPixel [part_number="Adafruit #1312"]
  Nano_Esqueleto_Secundario = Arduino Nano (Rev3.0)
  RDM6300_Sec_1 = IC, SIP package, 3 pins [chip_label=RFID]
  RDM6300_Sec_3 = IC, SIP package, 3 pins [chip_label=RFID]
  RDM6300_Sec_4 = IC, SIP package, 3 pins [chip_label=RFID]
  RDM6300_Sec_2 = IC, SIP package, 3 pins [chip_label=RFID]
  LED_SEC_CAJA = Adafruit Breadboard-Friendly NeoPixel [part_number="Adafruit #1312"]
  LED_SEC_RAYOS = Adafruit Breadboard-Friendly NeoPixel [part_number="Adafruit #1312"]
  Relay_Iman_Caja_Secundario = IC, DIP package, 6 pins [chip_label=Rele]
  Relay_Activacion_Murcielagos = IC, DIP package, 6 pins [chip_label=Rele]
  Relay_Iman_Caja_Primario = IC, DIP package, 6 pins [chip_label=Rele]
  Relay_Salida_Murcielagos = IC, DIP package, 6 pins [chip_label=Rele]

nets:
  P10: LED_PRIM_CAJA.IN, Nano_Esqueleto_Primario.D10
  GND: LED_PRIM_CAJA.GND, Nano_Esqueleto_Primario.GND, RDM6300_Prim_1.pin3, RDM6300_Prim_2.pin3, RDM6300_Prim_3.pin3, RDM6300_Prim_4.pin3, LED_PRIM_RAYOS.GND, Nano_Esqueleto_Secundario.GND, RDM6300_Sec_1.pin3, RDM6300_Sec_3.pin3, RDM6300_Sec_4.pin3, RDM6300_Sec_2.pin3, LED_SEC_RAYOS.GND, Relay_Iman_Caja_Secundario.pin3, Relay_Activacion_Murcielagos.pin3, Relay_Iman_Caja_Primario.pin3, Relay_Salida_Murcielagos.pin5
  5V: LED_PRIM_CAJA.VDD, RDM6300_Prim_1.pin1, LED_PRIM_RAYOS.VDD, LED_SEC_RAYOS.VDD
  P2: Nano_Esqueleto_Primario.D2, RDM6300_Prim_1.pin2
  P4: Nano_Esqueleto_Primario.D4, RDM6300_Prim_2.pin2
  P6: Nano_Esqueleto_Primario.D6, RDM6300_Prim_3.pin2
  P8: Nano_Esqueleto_Primario.D8, RDM6300_Prim_4.pin2
  P11: Nano_Esqueleto_Primario.D11/MOSI, LED_PRIM_RAYOS.IN
  P12: Nano_Esqueleto_Primario.D12/MISO, Relay_Iman_Caja_Primario.pin2
  PA5: Nano_Esqueleto_Primario.A5, LED_SEC_RAYOS.IN
  PA4: Nano_Esqueleto_Primario.A4, LED_SEC_CAJA.IN
  PA3: Nano_Esqueleto_Primario.A3, Relay_Salida_Murcielagos.pin4
  PA2: Nano_Esqueleto_Primario.A2, Relay_Activacion_Murcielagos.pin2
  S12: Nano_Esqueleto_Primario.A1, Nano_Esqueleto_Secundario.D12/MISO
  PA0: Nano_Esqueleto_Primario.A0, Relay_Iman_Caja_Secundario.pin2
  S2: Nano_Esqueleto_Secundario.D2, RDM6300_Sec_1.pin2
  S4: Nano_Esqueleto_Secundario.D4, RDM6300_Sec_2.pin2
  S6: Nano_Esqueleto_Secundario.D6, RDM6300_Sec_3.pin2
  S8: Nano_Esqueleto_Secundario.D8, RDM6300_Sec_4.pin2

notes:
  S12: Pin con el que el Secundario indica al Primario que se ha completado la fase RFID.
  Conectar COM a GND y NO al pin de activación de los Murciélagos.
  Este relay está controlado por los Murciélagos.

custom parts:
  Adafruit Breadboard-Friendly NeoPixel: This is the easiest way possible to add small, bright RGB pixels to your project. We took the same technology from our Flora NeoPixels and made them breadboard friendly, with two rows of 3 x 0.1" spaced header on each side for easy soldering, chaining and breadboarding. These ultra-bright LEDs have a constant-current driver cooked right into the LED package! The pixels are chainable - so you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
