# Fritzing sketch forja-dracula (saved by Fritzing 0.9.8b)
breadboards: 1

parts:
  Mega = Arduino Mega 2560 (Rev3)
  SENSOR_RGB_CARRIL_1 = Adafruit TCS34725 RGB Color Sensor [part_number="Adafruit #1334"]
  SENSOR_RGB_CARRIL_2 = Adafruit TCS34725 RGB Color Sensor [part_number="Adafruit #1334"]
  SENSOR_RGB_CARRIL_3 = Adafruit TCS34725 RGB Color Sensor [part_number="Adafruit #1334"]
  SENSOR_RGB_CARRIL_4 = Adafruit TCS34725 RGB Color Sensor [part_number="Adafruit #1334"]
  LED_CARRIL_1 = Neopixel Strip -- Black (30/m) [part_number=1376]
  LED_CARRIL_2 = Neopixel Strip -- Black (30/m) [part_number=1376]
  LED_CARRIL_3 = Neopixel Strip -- Black (30/m) [part_number=1376]
  LED_CARRIL_4 = Neopixel Strip -- Black (30/m) [part_number=1376]
  LED_BRASAS_CARRILES = Neopixel Strip -- Black (30/m) [part_number=1376]
  RFID_1 = ID-12_20 [package=id-12]
  RFID_2 = ID-12_20 [package=id-12]
  RFID_3 = ID-12_20 [package=id-12]
  RFID_4 = ID-12_20 [package=id-12]
  RFID_5 = ID-12_20 [package=id-12]
  KNOCK_1 = Piezo Speaker
  KNOCK_2 = Piezo Speaker
  R1 = Resistor [tolerance=±5% power=0.25 resistance=1M package=THT]
  R2 = Resistor [tolerance=±5% power=0.25 resistance=1M package=THT]
  LED_KNOCK_1 = Neopixel Strip -- Black (30/m) [part_number=1376]
  LED_KNOCK_2 = Neopixel Strip -- Black (30/m) [part_number=1376]

nets:
  A2: Mega.A2, KNOCK_1.pin2, R1.Pin_1
  A3: Mega.A3, KNOCK_2.pin2, R2.Pin_1
  D19: Mega.D19/RX1, RFID_1.D0
  D17: Mega.D17_PWM/RX2
  D15: Mega.D15/RX3
  GND: Mega.GND, SENSOR_RGB_CARRIL_1.GND, SENSOR_RGB_CARRIL_2.GND, SENSOR_RGB_CARRIL_3.GND, SENSOR_RGB_CARRIL_4.GND, LED_CARRIL_1.GND, LED_CARRIL_2.GND, LED_CARRIL_3.GND, LED_CARRIL_4.GND, LED_BRASAS_CARRILES.GND, RFID_1.GNDT, RFID_1.+_-, RFID_2.GNDT, RFID_2.+_-, RFID_3.GNDT, RFID_3.+_-, RFID_4.GNDT, RFID_4.+_-, RFID_5.GNDT, RFID_5.+_-, KNOCK_1.pin1, KNOCK_2.pin1, R1.Pin_0, R2.Pin_0, LED_KNOCK_1.GND, LED_KNOCK_2.GND
  D0: Mega.D0_RX0
  D3: Mega.D3_PWM
  D4: Mega.D4_PWM, LED_KNOCK_1.Din
  D5: Mega.D5_PWM, LED_KNOCK_2.Din
  D22: Mega.D22, SENSOR_RGB_CARRIL_1.SDA
  D23: Mega.D23, SENSOR_RGB_CARRIL_1.SCL
  D24: Mega.D24, SENSOR_RGB_CARRIL_2.SDA
  D25: Mega.D25, SENSOR_RGB_CARRIL_2.SCL
  D26: Mega.D26, SENSOR_RGB_CARRIL_3.SDA
  D27: Mega.D27, SENSOR_RGB_CARRIL_3.SCL
  D28: Mega.D28, SENSOR_RGB_CARRIL_4.SDA
  D29: Mega.D29, SENSOR_RGB_CARRIL_4.SCL
  D30: Mega.D30, LED_CARRIL_1.Din
  D31: Mega.D31, LED_CARRIL_2.Din
  D32: Mega.D32, LED_CARRIL_3.Din
  D33: Mega.D33, LED_CARRIL_4.Din
  D34: Mega.D34, LED_BRASAS_CARRILES.Din
  D38: Mega.D38, RFID_1.FUTURE
  D39: Mega.D39
  D40: Mega.D40
  D41: Mega.D41
  D42: Mega.D42
  5V: SENSOR_RGB_CARRIL_1.VIN, SENSOR_RGB_CARRIL_2.VIN, SENSOR_RGB_CARRIL_3.VIN, SENSOR_RGB_CARRIL_4.VIN, LED_CARRIL_1.+5V, LED_CARRIL_2.+5V, LED_CARRIL_3.+5V, LED_CARRIL_4.+5V, LED_BRASAS_CARRILES.+5V, RFID_1.5V, RFID_2.5V, RFID_3.5V, RFID_4.5V, RFID_5.5V, LED_KNOCK_1.+5V, LED_KNOCK_2.+5V

notes:
  Recordar: no se puede cargar programa con pin D0 (RX0) conectado

custom parts:
  Adafruit TCS34725 RGB Color Sensor: Your electronics can now see in dazzling color with this lovely color light sensor. We found the best color sensor on the market, the TCS34725, which has RGB and Clear light sensing elements. An IR blocking filter, integrated on-chip and localized to the color sensing photodiodes, minimizes the IR spectral component of the incoming light and allows color measurements to be made accurately. The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
  Neopixel Strip -- Black (30/m): These NeoPixel strips have 30 digitally-addressable pixel LEDs per meter and are very affordable and are only 12.5 mm wide, 10 mm if you remove the strip from the casing.
