# Fritzing sketch forja-dracula (saved by Fritzing 0.9.8b)
breadboards: 1

parts:
  Mega = Arduino Mega 2560 (Rev3)
  SENSOR_RGB_CARRIL_1 = Adafruit TCS34725 RGB Color Sensor [part_number="Adafruit #1334"]
  SENSOR_RGB_CARRIL_2 = Adafruit TCS34725 RGB Color Sensor [part_number="Adafruit #1334"]
  SENSOR_RGB_CARRIL_3 = Adafruit TCS34725 RGB Color Sensor [part_number="Adafruit #1334"]
  SENSOR_RGB_CARRIL_4 = Adafruit TCS34725 RGB Color Sensor [part_number="Adafruit #1334"]
  RFID_1 = ID-12_20 [package=id-12]
  RFID_2 = ID-12_20 [package=id-12]
  RFID_3 = ID-12_20 [package=id-12]
  RFID_4 = ID-12_20 [package=id-12]
  RFID_5 = ID-12_20 [package=id-12]
  KNOCK_1 = Piezo Speaker
  KNOCK_2 = Piezo Speaker
  R1 = Resistor [tolerance=±5% power=0.25 resistance=1M package=THT]
  R2 = Resistor [tolerance=±5% power=0.25 resistance=1M package=THT]
  LED_CARRIL_1 = Adafruit Breadboard-Friendly NeoPixel [part_number="Adafruit #1312"]
  LED_CARRIL_2 = Adafruit Breadboard-Friendly NeoPixel [part_number="Adafruit #1312"]
  LED_CARRIL_3 = Adafruit Breadboard-Friendly NeoPixel [part_number="Adafruit #1312"]
  LED_CARRIL_4 = Adafruit Breadboard-Friendly NeoPixel [part_number="Adafruit #1312"]
  LED_BRASAS_CARRILES = Adafruit Breadboard-Friendly NeoPixel [part_number="Adafruit #1312"]
  LED_KNOCK_1 = Adafruit Breadboard-Friendly NeoPixel [part_number="Adafruit #1312"]
  LED_KNOCK_2 = Adafruit Breadboard-Friendly NeoPixel [part_number="Adafruit #1312"]
  LED_PROGRESO = Adafruit Breadboard-Friendly NeoPixel [part_number="Adafruit #1312"]
  AUDIO_FX = Audio FX Sound Board
  LED_OJO_ODIN = Adafruit Breadboard-Friendly NeoPixel [part_number="Adafruit #1312"]

nets:
  A2: Mega.A2, KNOCK_1.pin2, R1.Pin_1
  A3: Mega.A3, KNOCK_2.pin2, R2.Pin_1
  D19: Mega.D19/RX1, RFID_1.D0
  D17: Mega.D17_PWM/RX2
  D15: Mega.D15/RX3
  GND: Mega.GND, SENSOR_RGB_CARRIL_1.GND, SENSOR_RGB_CARRIL_2.GND, SENSOR_RGB_CARRIL_3.GND, SENSOR_RGB_CARRIL_4.GND, RFID_1.GNDT, RFID_1.+_-, RFID_2.GNDT, RFID_2.+_-, RFID_3.GNDT, RFID_3.+_-, RFID_4.GNDT, RFID_4.+_-, RFID_5.GNDT, RFID_5.+_-, KNOCK_1.pin1, KNOCK_2.pin1, R1.Pin_0, R2.Pin_0, LED_CARRIL_1.GND, LED_CARRIL_2.GND, LED_CARRIL_3.GND, LED_CARRIL_4.GND, LED_BRASAS_CARRILES.GND, LED_KNOCK_1.GND, LED_KNOCK_2.GND, LED_PROGRESO.GND, AUDIO_FX.GND, LED_OJO_ODIN.GND
  D11: Mega.D11_PWM, AUDIO_FX.1
  D10: Mega.D10_PWM, AUDIO_FX.0
  D9: Mega.D9_PWM, AUDIO_FX.RST
  D8: Mega.D8_PWM, AUDIO_FX.ACT
  D0: Mega.D0_RX0
  D4: Mega.D4_PWM, LED_KNOCK_1.IN
  D5: Mega.D5_PWM, LED_KNOCK_2.IN
  D7: Mega.D7_PWM
  D22: Mega.D22, SENSOR_RGB_CARRIL_1.SDA
  D23: Mega.D23, SENSOR_RGB_CARRIL_1.SCL
  D24: Mega.D24, SENSOR_RGB_CARRIL_2.SDA
  D25: Mega.D25, SENSOR_RGB_CARRIL_2.SCL
  D26: Mega.D26, SENSOR_RGB_CARRIL_3.SDA
  D27: Mega.D27, SENSOR_RGB_CARRIL_3.SCL
  D28: Mega.D28, SENSOR_RGB_CARRIL_4.SDA
  D29: Mega.D29, SENSOR_RGB_CARRIL_4.SCL
  D30: Mega.D30, LED_CARRIL_1.IN
  D31: Mega.D31, LED_CARRIL_2.IN
  D32: Mega.D32, LED_CARRIL_3.IN
  D33: Mega.D33, LED_CARRIL_4.IN
  D34: Mega.D34, LED_BRASAS_CARRILES.IN
  D38: Mega.D38, RFID_1.FUTURE
  D39: Mega.D39
  D40: Mega.D40
  D41: Mega.D41
  D42: Mega.D42
  D50: Mega.D50, RFID_5.D0
  5V: SENSOR_RGB_CARRIL_1.VIN, SENSOR_RGB_CARRIL_2.VIN, SENSOR_RGB_CARRIL_3.VIN, SENSOR_RGB_CARRIL_4.VIN, RFID_1.5V, RFID_2.5V, RFID_3.5V, RFID_4.5V, RFID_5.5V, LED_CARRIL_1.VDD, LED_CARRIL_2.VDD, LED_CARRIL_3.VDD, LED_CARRIL_4.VDD, LED_BRASAS_CARRILES.VDD, LED_KNOCK_1.VDD, LED_KNOCK_2.VDD, LED_PROGRESO.VDD, AUDIO_FX.VIN, LED_OJO_ODIN.VDD
  D6: LED_PROGRESO.IN

notes:
  No se puede cargar programa con pin D0 (RX0) conectado
  No todos los pines del Mega soportan SoftwareSerial

custom parts:
  Adafruit TCS34725 RGB Color Sensor: Your electronics can now see in dazzling color with this lovely color light sensor. We found the best color sensor on the market, the TCS34725, which has RGB and Clear light sensing elements. An IR blocking filter, integrated on-chip and localized to the color sensing photodiodes, minimizes the IR spectral component of the incoming light and allows color measurements to be made accurately. The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
  Adafruit Breadboard-Friendly NeoPixel: This is the easiest way possible to add small, bright RGB pixels to your project. We took the same technology from our Flora NeoPixels and made them breadboard friendly, with two rows of 3 x 0.1" spaced header on each side for easy soldering, chaining and breadboarding. These ultra-bright LEDs have a constant-current driver cooked right into the LED package! The pixels are chainable - so you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
  Audio FX Sound Board: The Adafruit Sound Board, the fastest way to add audio effects to a project!
