# Fritzing sketch murcielagos (saved by Fritzing 0.9.8b)
breadboards: 1

parts:
  LED_OJOS_MURCIELAGOS = Adafruit Breadboard-Friendly NeoPixel [part_number="Adafruit #1312"]
  Nano_Esqueleto_Primario = Arduino Nano (Rev3.0)
  Relay_Salida_Murcielagos = IC, DIP package, 6 pins [chip_label=Rele]
  Relay_Activacion_Murcielagos = IC, DIP package, 6 pins [chip_label=Rele]
  R1 = Photocell (LDR) [package=THT]
  R2 = Resistor [tolerance=±5% resistance=10k package="1206 [SMD]"]
  R3 = Photocell (LDR) [package=THT]
  R4 = Resistor [tolerance=±5% resistance=10k package="1206 [SMD]"]
  R5 = Photocell (LDR) [package=THT]
  R6 = Resistor [tolerance=±5% resistance=10k package="1206 [SMD]"]
  R7 = Photocell (LDR) [package=THT]
  R8 = Resistor [tolerance=±5% resistance=10k package="1206 [SMD]"]
  R9 = Photocell (LDR) [package=THT]
  R10 = Resistor [tolerance=±5% resistance=10k package="1206 [SMD]"]
  R11 = Photocell (LDR) [package=THT]
  R12 = Resistor [tolerance=±5% resistance=10k package="1206 [SMD]"]
  R13 = Photocell (LDR) [package=THT]
  R14 = Resistor [tolerance=±5% resistance=10k package="1206 [SMD]"]
  J1 = Piezo Speaker
  R15 = Resistor [tolerance=±5% resistance=100 package="1206 [SMD]"]
  R16 = Resistor [tolerance=±5% resistance=100 package="1206 [SMD]"]
  J2 = Piezo Speaker
  R17 = Resistor [tolerance=±5% resistance=100 package="1206 [SMD]"]
  J3 = Piezo Speaker
  R18 = Resistor [tolerance=±5% resistance=100 package="1206 [SMD]"]
  J4 = Piezo Speaker
  R19 = Resistor [tolerance=±5% resistance=100 package="1206 [SMD]"]
  J5 = Piezo Speaker
  R20 = Resistor [tolerance=±5% resistance=100 package="1206 [SMD]"]
  J6 = Piezo Speaker
  R21 = Resistor [tolerance=±5% resistance=100 package="1206 [SMD]"]
  J7 = Piezo Speaker

nets:
  D10: LED_OJOS_MURCIELAGOS.IN, Nano_Esqueleto_Primario.D10
  GND: LED_OJOS_MURCIELAGOS.GND, Nano_Esqueleto_Primario.GND, Relay_Salida_Murcielagos.pin3, Relay_Activacion_Murcielagos.pin5, R2.Pin_0, R4.Pin_0, R6.Pin_0, R8.Pin_0, R10.Pin_0, R12.Pin_0, R14.Pin_0, J1.pin1, J2.pin1, J3.pin1, J4.pin1, J5.pin1, J6.pin1, J7.pin1
  5V: LED_OJOS_MURCIELAGOS.VDD, R1.pin_1, R3.pin_1, R5.pin_1, R7.pin_1, R9.pin_1, R11.pin_1, R13.pin_1
  D2: Nano_Esqueleto_Primario.D2, R15.Pin_1
  D3: Nano_Esqueleto_Primario.D3, R16.Pin_1
  D4: Nano_Esqueleto_Primario.D4, R17.Pin_1
  D5: Nano_Esqueleto_Primario.D5, R18.Pin_1
  D6: Nano_Esqueleto_Primario.D6, R19.Pin_1
  D7: Nano_Esqueleto_Primario.D7, R20.Pin_1
  D8: Nano_Esqueleto_Primario.D8, R21.Pin_1
  D11: Nano_Esqueleto_Primario.D11/MOSI, Relay_Activacion_Murcielagos.pin4
  D12: Nano_Esqueleto_Primario.D12/MISO, Relay_Salida_Murcielagos.pin2
  A6: Nano_Esqueleto_Primario.A6, R13.pin_0, R14.Pin_1
  A5: Nano_Esqueleto_Primario.A5, R11.pin_0, R12.Pin_1
  A4: Nano_Esqueleto_Primario.A4, R9.pin_0, R10.Pin_1
  A3: Nano_Esqueleto_Primario.A3, R7.pin_0, R8.Pin_1
  A2: Nano_Esqueleto_Primario.A2, R5.pin_0, R6.Pin_1
  A1: Nano_Esqueleto_Primario.A1, R3.pin_0, R4.Pin_1
  A0: Nano_Esqueleto_Primario.A0, R1.pin_0, R2.Pin_1
  N1: J1.pin2, R15.Pin_0
  N2: R16.Pin_0, J2.pin2
  N3: R17.Pin_0, J3.pin2
  N4: R18.Pin_0, J4.pin2
  N5: R19.Pin_0, J5.pin2
  N6: R20.Pin_0, J6.pin2
  N7: R21.Pin_0, J7.pin2

notes:
  Conectar COM a GND y NO al pin de salida de Murciélagos en el Esqueleto Primario.
  Este relay está controlado por el Esqueleto Primario.

custom parts:
  Adafruit Breadboard-Friendly NeoPixel: This is the easiest way possible to add small, bright RGB pixels to your project. We took the same technology from our Flora NeoPixels and made them breadboard friendly, with two rows of 3 x 0.1" spaced header on each side for easy soldering, chaining and breadboarding. These ultra-bright LEDs have a constant-current driver cooked right into the LED package! The pixels are chainable - so you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
