# Fritzing sketch velas (saved by Fritzing 0.9.8b)
breadboards: 1

parts:
  LED = Adafruit Breadboard-Friendly NeoPixel [part_number="Adafruit #1312"]
  Nano = Arduino Nano (Rev3.0)
  Boton_1 = Square Pushbutton
  Boton_2 = Square Pushbutton
  Boton_3 = Square Pushbutton
  Boton_4 = Square Pushbutton
  Boton_5 = Square Pushbutton
  Rele = IC, SIP package, 3 pins [chip_label=Rele]
  Boton_RESET = Square Pushbutton

nets:
  10: LED.IN, Nano.D10
  GND: LED.GND, Nano.GND, Boton_1.leg0, Rele.pin3
  5V: LED.VDD
  2: Nano.D2, Rele.pin2
  4: Nano.D4, Boton_1.leg1
  5: Nano.D5, Boton_2.leg1
  6: Nano.D6, Boton_3.leg1
  7: Nano.D7, Boton_4.leg1
  8: Nano.D8, Boton_5.leg1
  12: Nano.D12/MISO, Boton_RESET.leg1

custom parts:
  Adafruit Breadboard-Friendly NeoPixel: This is the easiest way possible to add small, bright RGB pixels to your project. We took the same technology from our Flora NeoPixels and made them breadboard friendly, with two rows of 3 x 0.1" spaced header on each side for easy soldering, chaining and breadboarding. These ultra-bright LEDs have a constant-current driver cooked right into the LED package! The pixels are chainable - so you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
