# Fritzing sketch teclado-gigante (saved by Fritzing 0.9.8b)
breadboards: 1

parts:
  Micro = Arduino Micro (Rev3)
  Multiplexor_1 = Analog Digital MUX Breakout
  Multiplexor_2 = Analog Digital MUX Breakout

nets:
  GND: Micro.GND, Multiplexor_1.GND, Multiplexor_1.EN, Multiplexor_2.GND, Multiplexor_2.EN
  D2: Micro.D2/SDA, Multiplexor_1.S3
  D3: Micro.D3/SCL, Multiplexor_1.S2
  D4: Micro.D4_PWM/A6, Multiplexor_1.S1
  D5: Micro.D5_PWM, Multiplexor_1.S0
  D7: Micro.D7, Multiplexor_2.S3
  D8: Micro.D8_PWM/A8, Multiplexor_2.S2
  D9: Micro.D9_PWM/A9, Multiplexor_2.S1
  D10: Micro.D10_PWM/A10, Multiplexor_2.S0
  5V: Micro.5V, Multiplexor_1.VCC, Multiplexor_2.VCC
  A1: Micro.A1, Multiplexor_2.SIG
  A0: Micro.A0, Multiplexor_1.SIG

notes:
  Ver correspondencia entre botones (C0, C1, etc) y alfabeto en programa
